# Fritzing sketch Sketch Shield Arduino ESP32 Wemos D1 L293D (saved by Fritzing 0.9.3b)
circuit board: 8.46667cm x 5.64444cm
perfboards: 1

parts:
  IC1 = L293D [package=THT]
  IC2 = L293D [package=THT]
  J1 = screw terminal, 5 pins
  J2 = screw terminal, 5 pins
  J3 = screw terminal, 3 pins  # not connected
  VCC1 = Battery block 9V
  S1 = Pushbutton [package="[THT]"]
  Arduino = Arduino Uno (Rev3)

nets (from the breadboard view):
  N1: IC1.Enable_1, Arduino.D5_PWM
  N2: IC1.In_1, Arduino.D6_PWM
  N3: IC1.Out_1_(_Controlled_by_Enable_1_), J1.pin1
  N4: IC1.0V, J1.pin3
  N5: IC1.Out_2_(_Controlled_by_Enable_1_), J1.pin2
  N6: IC1.In_2, Arduino.D7
  N7: IC1.+Vmotor, IC2.+Vmotor
  N8: IC1.Enable_2, Arduino.D3_PWM
  N9: IC1.In_3, Arduino.D2
  N10: IC1.Out_3_(_Controlled_by_Enable_2_), J1.pin5
  N11: IC1.Out_4_(_Controlled_by_Enable_2_), J1.pin4
  N12: IC1.In_4, Arduino.D4
  N13: IC2.Enable_1, Arduino.D11_PWM/MOSI
  N14: IC2.In_1, Arduino.D12/MISO
  N15: IC2.Out_1_(_Controlled_by_Enable_1_), J2.pin2
  N16: IC2.0V, J2.pin3
  N17: IC2.Out_2_(_Controlled_by_Enable_1_), J2.pin1
  N18: IC2.In_2, Arduino.D13/SCK
  N19: IC2.Enable_2, Arduino.D9_PWM
  N20: IC2.In_3, Arduino.D8
  N21: IC2.Out_3_(_Controlled_by_Enable_2_), J2.pin4
  N22: IC2.Out_4_(_Controlled_by_Enable_2_), J2.pin5
  N23: IC2.In_4, Arduino.D10_PWM/SS
  N24: VCC1.-, S1.Pin_1, S1.Pin_2
